// Logisim project 1.84.circ as structural Verilog: 5 circuits, main circuit 1.84b
module _1_84b (
  input  A,
  input  B,
  input  C,
  output AND,
  output NAND,
  output NORAND,
  output ORAND
);

  wire nand_1_out, nand_3_out, nand_4_out, nand_5_out, nand_6_out, nand_7_out, nand_8_out, nand_10_out,
       nand_11_out;

  nand nand_1 (nand_1_out, A, B);
  nand nand_2 (NAND, A, B);
  nand nand_3 (nand_3_out, A, A);
  nand nand_4 (nand_4_out, C, C);
  nand nand_5 (nand_5_out, B, B);
  nand nand_6 (nand_6_out, C, C);
  nand nand_7 (nand_7_out, C, C);
  nand nand_8 (nand_8_out, A, B);
  nand nand_9 (AND, nand_1_out, nand_1_out);
  nand nand_10 (nand_10_out, nand_3_out, nand_4_out);
  nand nand_11 (nand_11_out, nand_5_out, nand_6_out);
  nand nand_12 (ORAND, nand_7_out, nand_8_out);
  nand nand_13 (NORAND, nand_10_out, nand_11_out);
endmodule

module _1_84b_logik (
  input  A,
  input  B,
  input  C,
  output AND,
  output NAND,
  output NORAND,
  output ORAND
);

  wire and_2_out, and_3_out, and_4_out, not_1_out, not_2_out, not_3_out, not_4_out, not_5_out, not_6_out;

  and and_1 (AND, A, B);
  not not_1 (not_1_out, A);
  not not_2 (not_2_out, B);
  not not_3 (not_3_out, A);
  not not_4 (not_4_out, C);
  not not_5 (not_5_out, B);
  not not_6 (not_6_out, C);
  and and_2 (and_2_out, A, B);
  or or_1 (NAND, not_1_out, not_2_out);
  and and_3 (and_3_out, not_3_out, not_4_out);
  and and_4 (and_4_out, not_5_out, not_6_out);
  or or_2 (ORAND, C, and_2_out);
  or or_3 (NORAND, and_3_out, and_4_out);
endmodule

module _1_84c (
  input  A,
  input  B,
  input  C,
  output NOR,
  output N_OR_AND
);

  wire transistor_2_out, transistor_5_out, transistor_10_out;

  Transistor #(.\type ("n")) transistor_1 (.in(1'b0), .out(NOR), .gate(B));
  Transistor transistor_2 (.in(1'b1), .out(transistor_2_out), .gate(A));
  Transistor transistor_3 (.in(transistor_2_out), .out(NOR), .gate(B));
  Transistor #(.\type ("n")) transistor_4 (.in(1'b0), .out(NOR), .gate(A));
  Transistor transistor_5 (.in(1'b1), .out(transistor_5_out), .gate(NOR));
  Transistor #(.\type ("n")) transistor_6 (.in(1'b0), .out(transistor_5_out), .gate(NOR));
  Transistor transistor_7 (.in(1'b1), .out(N_OR_AND), .gate(transistor_5_out));
  Transistor transistor_8 (.in(1'b1), .out(N_OR_AND), .gate(C));
  Transistor #(.\type ("n")) transistor_9 (.in(transistor_10_out), .out(N_OR_AND), .gate(transistor_5_out));
  Transistor #(.\type ("n")) transistor_10 (.in(1'b0), .out(transistor_10_out), .gate(C));
  Transistor #(.\type ("n")) transistor_11 ();  // open: in, out, gate
  Transistor transistor_12 ();  // open: in, out, gate
endmodule

module _1_84c_logik (
  input  A,
  input  B,
  input  C,
  output NOR,
  output NORAND
);

  wire and_2_out, not_1_out, not_2_out, not_3_out, not_4_out, not_5_out;

  not not_1 (not_1_out, A);
  not not_2 (not_2_out, B);
  not not_3 (not_3_out, A);
  not not_4 (not_4_out, B);
  and and_1 (NOR, not_1_out, not_2_out);
  and and_2 (and_2_out, not_3_out, not_4_out);
  not not_5 (not_5_out, C);
  or or_1 (NORAND, and_2_out, not_5_out);
endmodule

module _1_84b_mod (
  input  A,
  input  B,
  input  C,
  output N_OR_AND
);

  wire transistor_1_out, transistor_6_out;

  Transistor transistor_1 (.in(1'b1), .out(transistor_1_out), .gate(A));
  Transistor transistor_2 (.in(1'b1), .out(transistor_1_out), .gate(B));
  Transistor transistor_3 (.in(transistor_1_out), .out(N_OR_AND), .gate(C));
  Transistor #(.\type ("n")) transistor_4 (.in(1'b0), .out(N_OR_AND), .gate(C));
  Transistor #(.\type ("n")) transistor_5 (.in(transistor_6_out), .out(N_OR_AND), .gate(A));
  Transistor #(.\type ("n")) transistor_6 (.in(1'b0), .out(transistor_6_out), .gate(B));
endmodule
