// Logisim project 1.85.circ as structural Verilog: 4 circuits, main circuit 1.85a
module _1_85a (
  input  A,
  input  B,
  input  C,
  output OR_NOT
);

  wire transistor_1_out, transistor_2_out;

  Transistor transistor_1 (.in(1'b1), .out(transistor_1_out), .gate(A));
  Transistor transistor_2 (.in(transistor_1_out), .out(transistor_2_out), .gate(B));
  Transistor transistor_3 (.in(transistor_2_out), .out(OR_NOT), .gate(C));
  Transistor #(.\type ("n")) transistor_4 (.in(1'b0), .out(OR_NOT), .gate(A));
  Transistor #(.\type ("n")) transistor_5 (.in(1'b0), .out(OR_NOT), .gate(B));
  Transistor #(.\type ("n")) transistor_6 (.in(1'b0), .out(OR_NOT), .gate(C));
endmodule

module _1_85b (
  input  A,
  input  B,
  input  C,
  output AND
);

  wire transistor_1_out, transistor_5_out, transistor_6_out;

  Transistor transistor_1 (.in(1'b1), .out(transistor_1_out), .gate(A));
  Transistor transistor_2 (.in(1'b1), .out(transistor_1_out), .gate(B));
  Transistor #(.\type ("n")) transistor_3 (.in(transistor_5_out), .out(transistor_1_out), .gate(A));
  Transistor transistor_4 (.in(1'b1), .out(transistor_1_out), .gate(C));
  Transistor #(.\type ("n")) transistor_5 (.in(transistor_6_out), .out(transistor_5_out), .gate(B));
  Transistor #(.\type ("n")) transistor_6 (.in(1'b0), .out(transistor_6_out), .gate(C));
  Transistor transistor_7 (.in(1'b1), .out(AND), .gate(transistor_1_out));
  Transistor #(.\type ("n")) transistor_8 (.in(1'b0), .out(AND), .gate(transistor_1_out));
endmodule

module _1_85c (
  input  A,
  input  B,
  output NOR,
  output OR
);

  wire transistor_1_out;

  Transistor transistor_1 (.in(1'b1), .out(transistor_1_out), .gate(A));
  Transistor transistor_2 (.in(1'b1), .out(OR), .gate(NOR));
  Transistor transistor_3 (.in(transistor_1_out), .out(NOR), .gate(B));
  Transistor #(.\type ("n")) transistor_4 (.in(1'b0), .out(NOR), .gate(A));
  Transistor #(.\type ("n")) transistor_5 (.in(1'b0), .out(OR), .gate(NOR));
  Transistor #(.\type ("n")) transistor_6 (.in(1'b0), .out(NOR), .gate(B));
endmodule

module _1_85clogic (
  input  A,
  input  B,
  output NOR,
  output OR
);

  wire not_1_out, not_2_out;

  not not_1 (not_1_out, A);
  not not_2 (not_2_out, B);
  or or_1 (OR, B, A);
  and and_1 (NOR, not_1_out, not_2_out);
endmodule
