// Logisim project 1.86.circ as structural Verilog: 2 circuits, main circuit 1.86
module _1_86 (
  input  A,
  input  B,
  input  C,
  output out_4
);

  wire transistor_1_out, transistor_3_out, transistor_5_out, transistor_8_out, transistor_9_out,
       transistor_12_out, transistor_15_out, transistor_19_out, transistor_20_out;

  Transistor transistor_1 (.in(1'b1), .out(transistor_1_out), .gate(A));
  Transistor transistor_2 (.in(1'b1), .out(transistor_1_out), .gate(B));
  Transistor transistor_3 (.in(1'b1), .out(transistor_3_out), .gate(B));
  Transistor transistor_4 (.in(1'b1), .out(transistor_3_out), .gate(C));
  Transistor transistor_5 (.in(1'b1), .out(transistor_5_out), .gate(C));
  Transistor transistor_6 (.in(1'b1), .out(transistor_5_out), .gate(A));
  Transistor #(.\type ("n")) transistor_7 (.in(transistor_9_out), .out(transistor_1_out), .gate(A));
  Transistor transistor_8 (.in(1'b1), .out(transistor_8_out), .gate(transistor_1_out));
  Transistor #(.\type ("n")) transistor_9 (.in(1'b0), .out(transistor_9_out), .gate(B));
  Transistor transistor_10 (.in(1'b1), .out(transistor_8_out), .gate(transistor_3_out));
  Transistor #(.\type ("n")) transistor_11 (.in(transistor_12_out), .out(transistor_3_out), .gate(B));
  Transistor #(.\type ("n")) transistor_12 (.in(1'b0), .out(transistor_12_out), .gate(C));
  Transistor #(.\type ("n")) transistor_13 (.in(transistor_15_out), .out(transistor_5_out), .gate(C));
  Transistor transistor_14 (.in(1'b1), .out(transistor_8_out), .gate(transistor_5_out));
  Transistor #(.\type ("n")) transistor_15 (.in(1'b0), .out(transistor_15_out), .gate(A));
  Transistor transistor_16 (.in(1'b1), .out(out_4), .gate(transistor_8_out));
  Transistor #(.\type ("n")) transistor_17 (.in(transistor_19_out), .out(transistor_8_out), .gate(transistor_1_out));
  Transistor #(.\type ("n")) transistor_18 (.in(1'b0), .out(out_4), .gate(transistor_8_out));
  Transistor #(.\type ("n")) transistor_19 (.in(transistor_20_out), .out(transistor_19_out), .gate(transistor_3_out));
  Transistor #(.\type ("n")) transistor_20 (.in(1'b0), .out(transistor_20_out), .gate(transistor_5_out));
endmodule

module _1_86_logic (
  input  A,
  input  B,
  input  C,
  output x
);

  wire and_1_out, and_2_out, and_3_out, not_1_out, not_2_out, not_3_out, not_4_out, not_5_out, not_6_out;

  not not_1 (not_1_out, A);
  not not_2 (not_2_out, B);
  not not_3 (not_3_out, A);
  not not_4 (not_4_out, C);
  not not_5 (not_5_out, B);
  not not_6 (not_6_out, C);
  and and_1 (and_1_out, not_1_out, not_2_out);
  and and_2 (and_2_out, not_3_out, not_4_out);
  and and_3 (and_3_out, not_5_out, not_6_out);
  or or_1 (x, and_1_out, and_2_out, and_3_out);
endmodule
