// Logisim project 1.89-1.90.circ as structural Verilog: 5 circuits, main circuit 1.89a RTL
module _1_89a_RTL (
  input  A,
  input  B,
  input  C,
  output OR_NOT
);

  Pull_Resistor #(.pull(1)) pull_resistor_1 (.node(OR_NOT));
  Transistor #(.\type ("n")) transistor_1 (.in(1'b0), .out(OR_NOT), .gate(A));
  Transistor #(.\type ("n")) transistor_2 (.in(1'b0), .out(OR_NOT), .gate(B));
  Transistor #(.\type ("n")) transistor_3 (.in(1'b0), .out(OR_NOT), .gate(C));
endmodule

module _1_89b_RTL (
  input  A,
  input  B,
  input  C,
  output AND_NOT
);

  wire transistor_2_out, transistor_3_out;

  Pull_Resistor #(.pull(1)) pull_resistor_1 (.node(AND_NOT));
  Transistor #(.\type ("n")) transistor_1 (.in(transistor_2_out), .out(AND_NOT), .gate(A));
  Transistor #(.\type ("n")) transistor_2 (.in(transistor_3_out), .out(transistor_2_out), .gate(B));
  Transistor #(.\type ("n")) transistor_3 (.in(1'b0), .out(transistor_3_out), .gate(C));
endmodule

module _1_89c_RTL (
  input  A,
  input  B,
  input  C,
  output AND_NOT,
  output AND
);

  wire transistor_3_out, transistor_4_out;

  Pull_Resistor #(.pull(1)) pull_resistor_1 (.node(AND_NOT));
  Transistor #(.\type ("n")) transistor_1 (.in(transistor_3_out), .out(AND_NOT), .gate(A));
  Pull_Resistor #(.pull(1)) pull_resistor_2 (.node(AND));
  Transistor #(.\type ("n")) transistor_2 (.in(1'b0), .out(AND), .gate(AND_NOT));
  Transistor #(.\type ("n")) transistor_3 (.in(transistor_4_out), .out(transistor_3_out), .gate(B));
  Transistor #(.\type ("n")) transistor_4 (.in(1'b0), .out(transistor_4_out), .gate(C));
endmodule

module Exp (
  input  A,
  input  B,
  input  C,
  output AND_NOT,
  output AND
);

  wire transistor_2_out, transistor_3_out;

  Pull_Resistor #(.pull(1)) pull_resistor_1 (.node(AND_NOT));
  Transistor #(.\type ("n")) transistor_1 (.in(transistor_2_out), .out(AND_NOT), .gate(A));
  Transistor #(.\type ("n")) transistor_2 (.in(transistor_3_out), .out(transistor_2_out), .gate(B));
  Transistor #(.\type ("n")) transistor_3 (.in(1'b0), .out(transistor_3_out), .gate(C));
  Transistor #(.\type ("n")) transistor_4 (.in(1'b0), .out(AND), .gate(AND_NOT));
endmodule

module _1_90 (
  input  A,
  input  B,
  input  C,
  output OR_NOT
);

  Pull_Resistor #(.pull(1)) pull_resistor_1 (.node(OR_NOT));
  Transistor #(.\type ("n")) transistor_1 (.in(1'b0), .out(OR_NOT), .gate(A));
  Transistor #(.\type ("n")) transistor_2 (.in(1'b0), .out(OR_NOT), .gate(B));
  Transistor #(.\type ("n")) transistor_3 (.in(1'b0), .out(OR_NOT), .gate(C));
endmodule
