// Logisim project K-MOP OR-NOT and OR.circ as structural Verilog: 1 circuit, main circuit main
module main (
  input  A,
  input  B,
  output OR_NOT,
  output OR
);

  wire transistor_1_out;

  Transistor transistor_1 (.in(1'b1), .out(transistor_1_out), .gate(A));
  Transistor transistor_2 (.in(transistor_1_out), .out(OR_NOT), .gate(B));
  Transistor #(.\type ("n")) transistor_3 (.in(1'b0), .out(OR_NOT), .gate(A));
  Transistor #(.\type ("n")) transistor_4 (.in(1'b0), .out(OR_NOT), .gate(B));
  Transistor transistor_5 (.in(1'b1), .out(OR), .gate(OR_NOT));
  Transistor #(.\type ("n")) transistor_6 (.in(1'b0), .out(OR), .gate(OR_NOT));
endmodule
